// Logisim project Main ALU.circ as structural Verilog: 1 circuit, main circuit Main
module Main (
  input  [3:0] A,
  input  [3:0] B,
  output Over,
  output Over_2,
  output [3:0] S,
  output [3:0] S_2
);

  Soma___4 soma_4_1 (.A(A), .out_3(Over), .B(B), .out_4(S));
  Sub___4 sub_4_1 (.A(A), .Vai_1(Over_2), .in_2(B), .out_4(S_2));
endmodule
